# Fritzing sketch operando (saved by Fritzing 0.9.3b)
breadboards: 1

parts:
  Componente1 = Arduino Mega 2560 (Rev3)
  LED1 = LED - 5mm [color="Red (633nm)" package="5 mm [THT]"]
  R1 = Resistor [tolerance=±5% resistance=220 package=THT]
  J1 = Piezo Speaker
  LED2 = RGB LED (com. cathode, rgb) [package="5 mm [THT]"]
  R2 = Resistor [tolerance=±5% resistance=220 package=THT]
  R3 = Resistor [tolerance=±5% resistance=220 package=THT]
  R4 = Resistor [tolerance=±5% resistance=220 package=THT]
  S1 = Pushbutton [package="[THT]"]
  R5 = Resistor [tolerance=±5% resistance=220 package=THT]
  S2 = Pushbutton [package="[THT]"]
  R6 = Resistor [tolerance=±5% resistance=220 package=THT]

nets:
  N1: Componente1.GND, R1.Pin_1, J1.pin1, LED2.common_cathode, R5.Pin_1, R6.Pin_1
  N2: Componente1.D10_PWM, S2.Pin_3, S2.Pin_4, R6.Pin_0
  N3: Componente1.D9_PWM, J1.pin2
  N4: Componente1.5V, S1.Pin_1, S1.Pin_2, S2.Pin_1, S2.Pin_2
  N5: Componente1.D3_PWM, R3.Pin_1
  N6: Componente1.D4_PWM, R2.Pin_0
  N7: Componente1.D5_PWM, R4.Pin_1
  N8: Componente1.D6_PWM, LED1.cathode
  N9: Componente1.D7_PWM, S1.Pin_3, S1.Pin_4, R5.Pin_0
  N10: LED1.anode, R1.Pin_0
  N11: LED2.red_anode, R2.Pin_1
  N12: LED2.green_anode, R3.Pin_0
  N13: LED2.blue_anode, R4.Pin_0

notes:
  El boton del pin 7 simula el toque con el borde (como en el juego)

// code stored in the sketch: operando.ino
#include <NonBlockingRtttl.h>

#define Buzzer 9

//Melodías en format RTTTL
const char * stranger = "StrangerThings:d=4,o=5,b=170:8c4,8p,8c4,8g,8b,8p,8c4,8p,8c4,8g,8e,8p,8c4,8p,8c4,8g,8b,8p,8c4,8p,8c4,8g,8e,8p,8c4,8p,8c4,8g,8b,8p,8c4,8p,8c4,8g,8e,8p,8c4,8p,8c4,8g,8b,8p,8c4,8p,8c4,8g,8e,8p,8p,8e4,8e,8g,8b,8p,8c4,8p,8c4,8g,8e,8p";
const char * halloween = "Halloween:d=4,o=5,b=180:8d6,8g,8g,8d6,8g,8g,8d6,8g,8d#6,8g,8d6,8g,8g,8d6,8g,8g,8d6,8g,8d#6,8g,8c#6,8f#,8f#,8c#6,8f#,8f#,8c#6,8f#,8d6,8f#,8c#6,8f#,8f#,8c#6,8f#,8f#,8c#6,8f#,8d6,8f#";

int LED = 6;
int Touch = 7;
int RESET = 10;

//Led RGB
int pinRojo = 4;
int pinVerde = 3;
int pinAzul = 5;

const int necessary_delay = 20; //milliseconds
bool isTouching = false;
unsigned long countStart;
int kill = 0;

void loopJuego() {
  unsigned long m = millis();

  digitalWrite(LED, isTouching);
  digitalWrite(Buzzer, isTouching);

  if (digitalRead(Touch) == HIGH) {
    if (isTouching) {
      countStart = m;
      return;
    }
    if (m - countStart >= necessary_delay) {
      countStart = m;
      kill++;
      cambiarColor(kill);
      Serial.println(kill);
      isTouching = true;
      return;
    }
  } else if (digitalRead(Touch) == LOW) {
    if (!isTouching) {
      countStart = m;
      return;
    }
    if (m - countStart >= necessary_delay) {
      countStart = m;
      isTouching = false;
      return;
    }
  }


}

//Colores
void setColor(int red, int green, int blue) {
  analogWrite(pinRojo, red);
  analogWrite(pinVerde, green);
  analogWrite(pinAzul, blue);
}

void cambiarColor(int kill) {
  
  if (kill > 1 && kill < 3) {
    setColor(52, 205, 255); //azul
  }
  if (kill > 2 && kill < 5) {
    setColor(118, 173, 253); //azul
  }
  if (kill > 4 && kill < 7) {
    setColor(0, 9, 228); //azul
  }
  if (kill > 6 && kill < 8) {
setColor(35, 85, 211); //azul
  }
  if (kill > 7 && kill < 10) {
    setColor(253, 0, 87); //morado
  }
  if (kill > 8) {
    setColor(179, 0, 223); //morado
  }
  if (kill > 9) {
    setColor(255, 0, 0); //rojo
  }
}

void setup() {
  pinMode(LED, OUTPUT);
  pinMode(Buzzer, OUTPUT);
  pinMode(Touch, INPUT);
  pinMode(RESET, INPUT);
  pinMode(pinRojo, OUTPUT);
  pinMode(pinVerde, OUTPUT);
  pinMode(pinAzul, OUTPUT);

  setColor(128, 128, 0); //Verde

  Serial.begin(115200);
  Serial.println();
}


void loop() {
  if (!rtttl::isPlaying()) {
    rtttl::begin(Buzzer, halloween);

    if (kill > 9) {
      rtttl::stop();
      rtttl::begin(Buzzer, stranger); //cambio de melodía
    }
  } else {
    rtttl::play();
  }

  loopJuego();
  
  //Si presionan RESET
  if(digitalRead(RESET) == HIGH){
    Serial.println("RESET");
    if(rtttl::isPlaying()){
      rtttl::stop();
      rtttl::begin(Buzzer, halloween); //cambio de melodía
      setColor(128, 128, 0); //Verde
      kill=0;
      delay(1000);
    }
  }  
}
